# Fritzing sketch MIDIDesk_v0.1 (saved by Fritzing 0.9.4)
circuit board: 8.55839cm x 4.78366cm
breadboards: 1

parts:
  U1 = Arduino Pro Micro (Clone)
  S1 = Momentary Switch [package=ksa_sealed_tac_switch]
  S2 = Momentary Switch [package=ksa_sealed_tac_switch]
  S3 = Momentary Switch [package=ksa_sealed_tac_switch]
  S5 = Momentary Switch [package=ksa_sealed_tac_switch]
  S6 = Momentary Switch [package=ksa_sealed_tac_switch]
  S7 = Momentary Switch [package=ksa_sealed_tac_switch]
  S8 = Momentary Switch [package=ksa_sealed_tac_switch]
  S4 = Momentary Switch [package=ksa_sealed_tac_switch]

nets:
  N1: U1.GND, S1.3, S1.4, S2.3, S2.4, S3.3, S3.4, S5.3, S5.4, S6.3, S6.4, S7.3, S7.4, S8.3, S8.4, S4.3, S4.4
  N2: U1.D6, S1.1, S1.2
  N3: U1.D7, S2.1, S2.2
  N4: U1.D8, S3.1, S3.2
  N5: U1.D9, S4.1, S4.2
  N6: U1.D10, S8.1, S8.2
  N7: U1.D16, S7.1, S7.2
  N8: U1.D14, S6.1, S6.2
  N9: U1.D15, S5.1, S5.2
